// Logisim project tp1.circ as structural Verilog: 1 circuit, main circuit main
module main (
  input  a,
  input  b,
  input  Y1,
  input  Y2,
  output L1,
  output L2,
  output out_7,
  output out_8
);

  wire and_1_out, and_6_out, and_7_out, and_8_out, and_9_out, and_10_out, clock_1_out, d_ff_1_q, d_ff_2_q,
       not_1_out, not_2_out, not_3_out, not_4_out, not_5_out, not_6_out, not_7_out, not_8_out, not_9_out,
       not_10_out, or_1_out, or_2_out, or_3_out, undriven;

  Clock clock_1 (.out(clock_1_out));
  not not_1 (not_1_out, Y2);
  not not_2 (not_2_out, d_ff_1_q);
  not not_3 (not_3_out, d_ff_2_q);
  not not_4 (not_4_out, d_ff_1_q);
  not not_5 (not_5_out, d_ff_2_q);
  or or_1 (or_1_out, Y1, not_1_out);
  not not_6 (not_6_out, b);
  not not_7 (not_7_out, Y1);
  and and_1 (and_1_out, b, a);
  and and_2 (L1, not_2_out, not_3_out);
  and and_3 (L2, not_4_out, d_ff_2_q);
  and and_4 (out_7, d_ff_1_q, d_ff_2_q);
  and and_5 (out_8, d_ff_1_q, not_5_out);
  and and_6 (and_6_out, b, a, or_1_out);
  and and_7 (and_7_out, not_7_out, Y2, b);
  not not_8 (not_8_out, b);
  not not_9 (not_9_out, Y1);
  not not_10 (not_10_out, Y1);
  and and_8 (and_8_out, not_6_out, Y1);
  and and_9 (and_9_out, Y2, not_8_out, not_9_out);
  and and_10 (and_10_out, not_10_out, a);
  or or_2 (or_2_out, and_6_out, and_8_out, and_7_out);
  or or_3 (or_3_out, and_9_out, and_10_out, and_1_out);
  D_Flip_Flop d_ff_1 (
    .clk(clock_1_out), .D(or_2_out), .Q(d_ff_1_q), .preset(undriven), .en(undriven));  // open: Qn, reset
  D_Flip_Flop d_ff_2 (.clk(clock_1_out), .D(or_3_out), .Q(d_ff_2_q));  // open: Qn, preset, en, reset

  // Notes on the sheet:
  //   y1
endmodule
